// Logisim project ObligatorioARQ.circ as structural Verilog: 1 circuit, main circuit main
module main (
  input  [11:0] in_1
);

  wire and_1_out, and_2_out, and_3_out, and_4_out, button_4_out, button_5_out, button_6_out, button_7_out,
       clock_1_out, decoder_1_out2, decoder_1_out3, decoder_1_out4, decoder_1_out5, or_1_out;
  wire [2:0] undriven;
  wire [4:0] counter_1_q;
  wire [11:0] shift_register_1_out, shift_register_2_out, shift_register_3_out, shift_register_4_out;

  Random #(.width(3)) RNG ();  // open: clk, next, out, clr
  Button button_1 ();  // open: out
  Button button_2 ();  // open: out
  Button button_3 ();  // open: out
  Decoder #(.select(3)) decoder_1 (
    .out2(decoder_1_out2), .out3(decoder_1_out3), .out4(decoder_1_out4), .out5(decoder_1_out5), .sel(undriven));  // open: out0, out1, out6, out7, en
  Clock clock_1 (.out(clock_1_out));
  LED led_1 ();  // open: in
  LED led_2 ();  // open: in
  LED led_3 ();  // open: in
  Shift_Register #(.length(12)) shift_register_1 (
    .in(decoder_1_out2), .clk(clock_1_out), .out(shift_register_1_out[0]), .q0(shift_register_1_out[11]),
    .q1(shift_register_1_out[10]), .q2(shift_register_1_out[9]), .q3(shift_register_1_out[8]),
    .q4(shift_register_1_out[7]), .q5(shift_register_1_out[6]), .q6(shift_register_1_out[5]),
    .q7(shift_register_1_out[4]), .q8(shift_register_1_out[3]), .q9(shift_register_1_out[2]),
    .q10(shift_register_1_out[1]));  // open: shift, load, clr, d0, d1, d2, d3, d4, d5, d6, d7, d8, d9, d10, d11, q11
  Shift_Register #(.length(12)) shift_register_2 (
    .in(decoder_1_out3), .clk(clock_1_out), .out(shift_register_2_out[0]), .q0(shift_register_2_out[11]),
    .q1(shift_register_2_out[10]), .q2(shift_register_2_out[9]), .q3(shift_register_2_out[8]),
    .q4(shift_register_2_out[7]), .q5(shift_register_2_out[6]), .q6(shift_register_2_out[5]),
    .q7(shift_register_2_out[4]), .q8(shift_register_2_out[3]), .q9(shift_register_2_out[2]),
    .q10(shift_register_2_out[1]));  // open: shift, load, clr, d0, d1, d2, d3, d4, d5, d6, d7, d8, d9, d10, d11, q11
  Shift_Register #(.length(12)) shift_register_3 (
    .in(decoder_1_out4), .clk(clock_1_out), .out(shift_register_3_out[0]), .q0(shift_register_3_out[11]),
    .q1(shift_register_3_out[10]), .q2(shift_register_3_out[9]), .q3(shift_register_3_out[8]),
    .q4(shift_register_3_out[7]), .q5(shift_register_3_out[6]), .q6(shift_register_3_out[5]),
    .q7(shift_register_3_out[4]), .q8(shift_register_3_out[3]), .q9(shift_register_3_out[2]),
    .q10(shift_register_3_out[1]));  // open: shift, load, clr, d0, d1, d2, d3, d4, d5, d6, d7, d8, d9, d10, d11, q11
  Shift_Register #(.length(12)) shift_register_4 (
    .in(decoder_1_out5), .clk(clock_1_out), .out(shift_register_4_out[0]), .q0(shift_register_4_out[11]),
    .q1(shift_register_4_out[10]), .q2(shift_register_4_out[9]), .q3(shift_register_4_out[8]),
    .q4(shift_register_4_out[7]), .q5(shift_register_4_out[6]), .q6(shift_register_4_out[5]),
    .q7(shift_register_4_out[4]), .q8(shift_register_4_out[3]), .q9(shift_register_4_out[2]),
    .q10(shift_register_4_out[1]));  // open: shift, load, clr, d0, d1, d2, d3, d4, d5, d6, d7, d8, d9, d10, d11, q11
  DotMatrix #(.matrixcols(9), .matrixrows(12)) dotmatrix_1 (
    .col0(in_1), .col1(shift_register_1_out), .col2(in_1), .col3(shift_register_2_out), .col4(in_1),
    .col5(shift_register_3_out), .col6(in_1), .col7(shift_register_4_out), .col8(in_1));
  LED led_4 ();  // open: in
  Button button_4 (.out(button_4_out));
  Button button_5 (.out(button_5_out));
  and and_1 (and_1_out, button_4_out, shift_register_1_out[2]);
  and and_2 (and_2_out, button_5_out, shift_register_2_out[2]);
  and and_3 (and_3_out, button_6_out, shift_register_3_out[2]);
  and and_4 (and_4_out, button_7_out, shift_register_4_out[2]);
  LED led_5 ();  // open: in
  LED led_6 ();  // open: in
  LED led_7 ();  // open: in
  LED led_8 ();  // open: in
  Button button_6 (.out(button_6_out));
  Button button_7 (.out(button_7_out));
  LED led_9 ();  // open: in
  LED led_10 ();  // open: in
  LED led_11 ();  // open: in
  or or_1 (or_1_out, and_1_out, and_2_out, and_3_out, and_4_out);
  _7_Segment_Display u_7_segment_display_1 ();  // open: g, f, a, b, e, d, c, dp
  Counter #(.max('h1f), .width(5)) counter_1 (.Q(counter_1_q), .clk(or_1_out));  // open: load, D, count, carry, up, clr
  _7_Segment_Display u_7_segment_display_2 ();  // open: g, f, a, b, e, d, c, dp
  _7_Segment_Display u_7_segment_display_3 ();  // open: g, f, a, b, e, d, c, dp

  // Notes on the sheet:
  //   Esperando modo
  //   Jugando
  //   Grabando
  //   ____
  //   :
endmodule
